# Fritzing sketch GCController (saved by Fritzing 0.9.2b)
circuit board: 8.46667cm x 5.64444cm
breadboards: 1

parts:
  Part1 = Arduino Uno (Rev3)
  Q1 = NPN-Transistor [package="TO92 [THT]"]
  R1 = Resistor [tolerance=±5% resistance=330 package=THT]
  R2 = Resistor [tolerance=±5% resistance=10k package=THT]
  J1 = female pin header, 5 pins [form="♀ (female)" part_number="GC controller cable"]

nets:
  N1: Part1.D8, R2.Pin_0
  N2: Part1.GND, Q1.C, J1.pin3, J1.pin4
  N3: Part1.D4, Q1.E, R1.Pin_0, J1.pin2
  N4: Part1.3V3, R1.Pin_1, J1.pin1
  N5: Q1.B, R2.Pin_1
